# Fritzing sketch SynthByte (saved by Fritzing 0.7.5b)
breadboards: 1

parts:
  Arduino1 = Arduino
  R1 = Resistor [tolerance=±5% resistance=1k package=THT]
  R2 = Resistor [tolerance=±5% resistance=1k package=THT]
  R3 = Resistor [tolerance=±5% resistance=1k package=THT]
  R5 = Resistor [tolerance=±5% resistance=1k package=THT]
  R6 = Resistor [tolerance=±5% resistance=1k package=THT]
  LED1 = LED - 5mm [color="Green (555nm)" package="5 mm [THT]"]
  LED2 = LED - 5mm [color="Green (555nm)" package="5 mm [THT]"]
  LED3 = LED - 5mm [color="Yellow (595nm)" package="5 mm [THT]"]
  LED4 = LED - 5mm [color="Yellow (595nm)" package="5 mm [THT]"]
  LED5 = LED - 5mm [color="Red (633nm)" package="5 mm [THT]"]
  LED6 = LED - 5mm [color="Red (633nm)" package="5 mm [THT]"]
  J1 = Piezo Speaker
  R8 = Resistor [tolerance=±5% resistance=390 package=THT]
  C1 = Tantalum Capacitor [capacitance=0.01µF package="100 mil [THT, tantalum]"]
  R9 = Rotary Potentiometer (Small) [maximum_resistance=100kΩ]
  R10 = Rotary Potentiometer (Small) [maximum_resistance=100kΩ]
  S2 = Pushbutton [package=THT]
  S3 = Pushbutton [package=THT]
  S1 = Pushbutton [package=THT]
  R7 = Resistor [tolerance=±5% resistance=10k package=THT]
  S4 = Pushbutton [package=THT]
  R4 = Resistor [tolerance=±5% resistance=1k package=THT]
  J2 = female pin header, 2 pins [form="♀ (female)"]
  TRS1 = Audio Jack (TRS) 3.5mm [package="4Ucon 08780 [THT]"]

nets:
  N1: Arduino1.GND, LED1.cathode, LED2.cathode, LED3.cathode, LED4.cathode, LED5.cathode, LED6.cathode, J1.pin1, C1.-, R9.leg1, R10.leg1, S2.leg1, S3.leg1, S1.leg1, S4.leg1, J2.pin2, TRS1.Tip
  N2: Arduino1.D12, S4.leg0
  N3: Arduino1.D11, R8.Pin_0, R7.Pin_0
  N4: Arduino1.D10, R6.Pin_0
  N5: Arduino1.D9, R5.Pin_0
  N6: Arduino1.D8, S3.leg0
  N7: Arduino1.D7, S2.leg0
  N8: Arduino1.D6, R4.Pin_0
  N9: Arduino1.D5, R3.Pin_0
  N10: Arduino1.D4, S1.leg0
  N11: Arduino1.D3, R2.Pin_0
  N12: Arduino1.D2, R1.Pin_0
  N13: Arduino1.+5V, R9.leg2, R10.leg2
  N14: Arduino1.A4, R9.wiper
  N15: Arduino1.A5, R10.wiper
  N16: R1.Pin_1, LED1.anode
  N17: R2.Pin_1, LED2.anode
  N18: R3.Pin_1, LED3.anode
  N19: R5.Pin_1, LED5.anode
  N20: R6.Pin_1, LED6.anode
  N21: LED4.anode, R4.Pin_1
  N22: J1.pin2, R8.Pin_1, TRS1.Sleeve
  N23: C1.+, R7.Pin_1, J2.pin1
